// Logisim project 16-bit Computer.circ as structural Verilog: 3 circuits, main circuit main
module main (
  input  [15:0] Bus_Override,
  input  in_2,
  input  Power,
  input  Manual_Override,
  input  AX_In,
  input  BX_In,
  input  CX_In,
  input  DX_In,
  input  ALU_Out,
  input  [3:0] Op_Sel,
  input  Reg,
  input  Out,
  input  in_13,
  input  RAM_Out,
  input  RAM_In,
  output out_16,
  output out_17,
  output out_18,
  output out_19,
  output out_20,
  output out_21,
  output out_22,
  output out_23,
  output out_24,
  output out_25,
  output out_26,
  output out_27,
  output out_28,
  output out_29,
  output out_30,
  output out_31
);

  wire Clock_out, Manual_Tick_out;
  wire [15:0] A_q, alu_1_alu_out, and_1_out, and_2_out, and_3_out, and_4_out, and_5_out, and_6_out,
       and_7_out, AX_q, B_q, BX_q, CX_q, DX_q, MAR_q, or_2_out, ram_1_data;
  wire [15:15] rom_1_data, rom_1_data_2, rom_1_data_3, rom_1_data_4;

  Button Manual_Tick (.out(Manual_Tick_out));
  assign and_1_out = Bus_Override & {16{in_2}};  // AND_Gate and_1, 16 bits wide
  Clock Clock (.Power(Power), .Manual_Override(Manual_Override), .Manual_Tick(Manual_Tick_out), .Out(Clock_out));
  ALU alu_1 (.Operation(Op_Sel), .A(A_q), .B(B_q), .ALU_Out(alu_1_alu_out));
  Register #(.width(16)) A (
    .D({out_16, out_17, out_18, out_19, out_20, out_21, out_22, out_23, out_24, out_25, out_26, out_27, out_28, out_29, out_30, out_31}),
    .Q(A_q), .clk(Clock_out));  // open: en, clr
  Register #(.width(16)) B (
    .D({out_16, out_17, out_18, out_19, out_20, out_21, out_22, out_23, out_24, out_25, out_26, out_27, out_28, out_29, out_30, out_31}),
    .Q(B_q), .clk(Clock_out));  // open: en, clr
  assign {out_16, out_17, out_18, out_19, out_20, out_21, out_22, out_23, out_24, out_25, out_26, out_27, out_28, out_29, out_30, out_31} = and_1_out | and_2_out | and_7_out | or_2_out;  // OR_Gate or_1, 16 bits wide
  assign and_2_out = {16{ALU_Out}} & alu_1_alu_out;  // AND_Gate and_2, 16 bits wide
  assign or_2_out = and_3_out | and_4_out | and_5_out | and_6_out;  // OR_Gate or_2, 16 bits wide
  assign and_3_out = {16{rom_1_data[15]}} & DX_q;  // AND_Gate and_3, 16 bits wide
  assign and_4_out = {16{rom_1_data_2[15]}} & CX_q;  // AND_Gate and_4, 16 bits wide
  assign and_5_out = {16{rom_1_data_3[15]}} & BX_q;  // AND_Gate and_5, 16 bits wide
  assign and_6_out = {16{rom_1_data_4[15]}} & AX_q;  // AND_Gate and_6, 16 bits wide
  Register #(.width(16)) MAR (
    .D({out_16, out_17, out_18, out_19, out_20, out_21, out_22, out_23, out_24, out_25, out_26, out_27, out_28, out_29, out_30, out_31}),
    .en(in_13), .Q(MAR_q), .clk(Clock_out));  // open: clr
  Register #(.width(16)) AX (
    .D({out_16, out_17, out_18, out_19, out_20, out_21, out_22, out_23, out_24, out_25, out_26, out_27, out_28, out_29, out_30, out_31}),
    .en(AX_In), .Q(AX_q), .clk(Clock_out));  // open: clr
  assign and_7_out = {16{RAM_Out}} & ram_1_data;  // AND_Gate and_7, 16 bits wide
  RAM #(.addrWidth(16), .dataWidth(16), .bus("separate")) ram_1 (
    .addr(MAR_q),
    .din({out_16, out_17, out_18, out_19, out_20, out_21, out_22, out_23, out_24, out_25, out_26, out_27, out_28, out_29, out_30, out_31}),
    .data(ram_1_data), .str(RAM_In), .clk(Clock_out));  // open: sel, ld, clr
  Register #(.width(16)) BX (
    .D({out_16, out_17, out_18, out_19, out_20, out_21, out_22, out_23, out_24, out_25, out_26, out_27, out_28, out_29, out_30, out_31}),
    .en(BX_In), .Q(BX_q), .clk(Clock_out));  // open: clr
  Register #(.width(16)) DX (
    .D({out_16, out_17, out_18, out_19, out_20, out_21, out_22, out_23, out_24, out_25, out_26, out_27, out_28, out_29, out_30, out_31}),
    .en(DX_In), .Q(DX_q), .clk(Clock_out));  // open: clr
  Register #(.width(16)) CX (
    .D({out_16, out_17, out_18, out_19, out_20, out_21, out_22, out_23, out_24, out_25, out_26, out_27, out_28, out_29, out_30, out_31}),
    .en(CX_In), .Q(CX_q), .clk(Clock_out));  // open: clr
  ROM #(.addrWidth(2), .dataWidth(4)) rom_1 (
    .addr({Out, Reg}), .data({rom_1_data[15], rom_1_data_2[15], rom_1_data_3[15], rom_1_data_4[15]}));  // open: sel

  // Notes on the sheet:
  //   RAM
  //   contents of rom_1 (hex, n*v repeats v):
  //   1 2 4 8
endmodule

module Clock (
  input  Power,
  input  Manual_Override,
  input  Manual_Tick,
  output Out
);

  wire and_1_out, and_2_out, clock_1_out, not_1_out, or_1_out;

  Clock_part clock_1 (.out(clock_1_out));
  not not_1 (not_1_out, Manual_Override);
  and and_1 (and_1_out, not_1_out, clock_1_out);
  and and_2 (and_2_out, Manual_Override, Manual_Tick);
  or or_1 (or_1_out, and_1_out, and_2_out);
  and and_3 (Out, Power, or_1_out);
endmodule

module ALU (
  input  [3:0] Operation,
  input  [15:0] A,
  input  [15:0] B,
  output [15:0] ALU_Out
);

  wire [15:0] adder_1_out, and_1_out, divider_1_out, multiplier_1_out, nand_1_out, nor_1_out, not_1_out,
       or_1_out, shifter_1_out, shifter_2_out, shifter_3_out, shifter_4_out, shifter_5_out, subtractor_1_out,
       xnor_1_out, xor_1_out;

  Adder #(.width(16)) adder_1 (.a(A), .b(B), .out(adder_1_out));  // open: cin, cout
  Subtractor #(.width(16)) subtractor_1 (.a(A), .b(B), .out(subtractor_1_out));  // open: bin, bout
  Multiplier #(.width(16)) multiplier_1 (.a(A), .b(B), .out(multiplier_1_out));  // open: cin, cout
  Divider #(.width(16)) divider_1 (.a(A), .b(B), .out(divider_1_out));  // open: upper, rem
  Shifter #(.width(16)) shifter_1 (.in(A), .\dist (B[3:0]), .out(shifter_1_out));
  Shifter #(.width(16), .shift("lr")) shifter_2 (.in(A), .\dist (B[3:0]), .out(shifter_2_out));
  Shifter #(.width(16), .shift("ar")) shifter_3 (.in(A), .\dist (B[3:0]), .out(shifter_3_out));
  Shifter #(.width(16), .shift("rl")) shifter_4 (.in(A), .\dist (B[3:0]), .out(shifter_4_out));
  Shifter #(.width(16), .shift("rr")) shifter_5 (.in(A), .\dist (B[3:0]), .out(shifter_5_out));
  assign and_1_out = A & B;  // AND_Gate and_1, 16 bits wide
  assign or_1_out = A | B;  // OR_Gate or_1, 16 bits wide
  assign xor_1_out = A ^ B;  // XOR_Gate xor_1, 16 bits wide
  assign not_1_out = ~A;  // NOT_Gate not_1, 16 bits wide
  assign nand_1_out = ~(A & B);  // NAND_Gate nand_1, 16 bits wide
  assign nor_1_out = ~(A | B);  // NOR_Gate nor_1, 16 bits wide
  assign xnor_1_out = ~(A ^ B);  // XNOR_Gate xnor_1, 16 bits wide
  Multiplexer #(.select(4), .width(16), .disabled(0), .enable("false")) multiplexer_1 (
    .in0(adder_1_out), .in1(subtractor_1_out), .in2(multiplier_1_out), .in3(divider_1_out),
    .in4(shifter_1_out), .in5(shifter_2_out), .in6(shifter_3_out), .in7(shifter_4_out), .in8(shifter_5_out),
    .in9(and_1_out), .in10(or_1_out), .in11(xor_1_out), .in12(not_1_out), .in13(nand_1_out),
    .in14(nor_1_out), .in15(xnor_1_out), .out(ALU_Out), .sel(Operation));
endmodule
